# Fritzing sketch arduino (saved by Fritzing 0.7.1b)
breadboards: 1

parts:
  LCD1 = LCD screen
  Pad1 = Pad [width=80 height=5 connect=center]  # not connected
  Arduino1 = Arduino
  R1 = Resistor [tolerance=±5% resistance=10k package=THT]
  R2 = Resistor [tolerance=±5% resistance=1k package=THT]
  R3 = Resistor [tolerance=±5% resistance=150 package=THT]

nets:
  VSS: LCD1.VSS, LCD1.R/W, LCD1.LED-, Arduino1.GND, R2.Pin_0
  VDD: LCD1.VDD, Arduino1.+5V, R1.Pin_0, R3.Pin_0
  N1: LCD1.V0, R1.Pin_1, R2.Pin_1
  N2: LCD1.RS, Arduino1.D12
  N3: LCD1.E, Arduino1.D11
  N4: LCD1.DB0, Arduino1.D2
  N5: LCD1.DB1, Arduino1.D3
  N6: LCD1.DB2, Arduino1.D4
  N7: LCD1.DB3, Arduino1.D5
  N8: LCD1.DB4, Arduino1.D6
  N9: LCD1.DB5, Arduino1.D7
  N10: LCD1.DB6, Arduino1.D8
  N11: LCD1.DB7, Arduino1.D9
  N12: LCD1.LED+, R3.Pin_1

notes:
  NMEA+
