# Fritzing sketch bare_atmega (saved by Fritzing 0.7.1b)
breadboards: 1

parts:
  U1 = atmega168 [package=dip]
  U2 = Voltage Regulator - 5V [package="TO220 [THT]"]
  C2 = Ceramic Capacitor [capacitance=330nF package="100 mil [THT, multilayer]"]
  C1 = Ceramic Capacitor [capacitance=100nF package="200 mil [THT, multilayer]"]
  LCD1 = LCD screen
  J1 = Screw terminal - 2 pins [package=THT]
  R1 = Resistor [tolerance=±5% resistance=1k package=THT]
  R2 = Resistor [tolerance=±5% resistance=10k package=THT]
  R3 = Resistor [tolerance=±5% resistance=120 package=THT]
  XTAL1 = Crystal [frequency="16 Mhz" package=THT]
  J2 = Screw terminal - 2 pins [package=THT]
  C3 = Ceramic Capacitor [capacitance=22pF package="100 mil [THT, multilayer]"]
  C4 = Ceramic Capacitor [capacitance=22pF package="100 mil [THT, multilayer]"]
  Pad1 = Pad [width=80 height=5 connect=center]  # not connected

nets:
  VCC: U1.RESET, U1.VCC, U1.AVCC, U2.output_voltage, C1.0, LCD1.VDD, R2.Pin_0, R3.Pin_0
  N1: U1.D0_(RX), J1.pin1
  N2: U1.D1_(TX), J1.pin2
  N3: U1.D2, LCD1.DB0
  N4: U1.D3_(PWM), LCD1.DB1
  N5: U1.D4, LCD1.DB2
  GND: U1.GND, U2.GND, C2.0, C1.1, LCD1.VSS, LCD1.R/W, LCD1.LED-, R1.Pin_0, J2.pin2, C3.1, C4.1
  N6: U1.XLAT1, XTAL1.pin_0, C3.0
  N7: U1.XLAT2, XTAL1.pin_1, C4.0
  N8: U1.D5_(PWM), LCD1.DB3
  N9: U1.D6_(PWM), LCD1.DB4
  N10: U1.D7, LCD1.DB5
  N11: U1.D8, LCD1.DB6
  N12: U1.D9_(PWM), LCD1.DB7
  N13: U1.D11_(PWM), LCD1.E
  N14: U1.D12, LCD1.RS
  N15: U2.input_voltage, C2.1, J2.pin1
  N16: LCD1.V0, R1.Pin_1, R2.Pin_1
  N17: LCD1.LED+, R3.Pin_1
